# Fritzing sketch ProjetoCofre (saved by Fritzing 0.9.3b)
breadboards: 1

parts:
  Componente1 = Arduino Mega ADK (Rev3)
  BT1 = Bluetooth HC-06u [package=THT]
  R1 = Resistor [tolerance=±5% resistance=1k package="0402 [SMD]"]
  R2 = Resistor [tolerance=±5% resistance=1k package="0402 [SMD]"]
  R3 = Resistor [tolerance=±5% resistance=1k package="0402 [SMD]"]
  S1 = Pushbutton [package="[SMD]"]
  S2 = Pushbutton [package="[SMD]"]
  S3 = Pushbutton [package="[SMD]"]
  S4 = Pushbutton [package="[SMD]"]
  S5 = Pushbutton [package="[SMD]"]
  S6 = Pushbutton [package="[SMD]"]

nets:
  N1: Componente1.D13_PWM, S6.Pin_3, S6.Pin_4
  N2: Componente1.D12_PWM, S5.Pin_3, S5.Pin_4
  N3: Componente1.D11_PWM, S2.Pin_3, S2.Pin_4
  N4: Componente1.D10_PWM, S3.Pin_3, S3.Pin_4
  N5: Componente1.D9_PWM, S4.Pin_3, S4.Pin_4
  N6: Componente1.D8_PWM, S1.Pin_3, S1.Pin_4
  5V: Componente1.5V, BT1.VCC
  GND: Componente1.GND, BT1.GND, R1.Pin_1, S1.Pin_1, S1.Pin_2, S2.Pin_1, S2.Pin_2, S3.Pin_1, S3.Pin_2, S4.Pin_1, S4.Pin_2, S5.Pin_1, S5.Pin_2, S6.Pin_1, S6.Pin_2
  N7: Componente1.D6_PWM, BT1.TXD
  N8: Componente1.D7_PWM, BT1.RXD, R3.Pin_0
  N9: R1.Pin_0, R2.Pin_1
  N10: R2.Pin_0, R3.Pin_1

custom parts:
  Bluetooth HC-06u: Bluetooth HC-06 - face up, pins down 16.5mm x 37.5mm PCB
